# Fritzing sketch webplant (saved by Fritzing 0.9.5d)
breadboards: 1

parts:
  Raspberry_Pi_1 = Raspberry Pi 3 [part_number=RPI-3-V1.2]  # not connected
  Part1 = Arduino Uno (Rev3)
  RHT1 = Humidity and Temperature Sensor RHT03
  Part2 = Soil Moisture Sensor
  LED1 = LED - 5mm [color="Red (633nm)" package="5 mm [THT]"]
  LED2 = LED - 5mm [color="Green (555nm)" package="5 mm [THT]"]
  LED3 = LED - 5mm [color="Yellow (595nm)" package="5 mm [THT]"]

nets:
  N1: Part1.A0, Part2.SIG
  N2: Part1.D8, RHT1.Data-signal
  N3: Part1.D5_PWM, LED2.anode
  N4: Part1.D6_PWM, LED3.anode
  N5: Part1.D7, LED1.anode
  VCC: Part1.3V3, RHT1.Vcc, Part2.VCC
  GND: Part1.GND, RHT1.GND_2, Part2.GND, LED1.cathode, LED2.cathode, LED3.cathode

notes:
  Arduino dihubungkan ke RPI melalui port USB
